// Logisim project lab6ssss.circ as structural Verilog: 29 circuits, main circuit main
// byte2
module main (
  output [3:0] out_1,
  output [2:0] out_2,
  output out_3,
  output [63:0] showRAX,
  output [63:0] showRCX,
  output [63:0] showRDX,
  output [63:0] showRBX,
  output [63:0] showRSP,
  output [63:0] showRBP,
  output [63:0] showRSI,
  output [63:0] showRDI,
  output [63:0] showR8,
  output [63:0] showR9,
  output [63:0] showR10,
  output [63:0] showR11,
  output [63:0] showR12,
  output [11:0] out_17,
  output [63:0] showR13,
  output [63:0] showR14
);

  wire and_1_out, clock_1_out, execute_1_condsignal, fetch_1_notvalid;
  wire [3:0] fetch_1_ifun, fetch_1_ra, fetch_1_rb;
  wire [11:0] fetch_1_valp, pcupdate_1_newpc;
  wire [63:0] decode_1_vala, decode_1_valb, execute_1_vale, fetch_1_valc, memory_1_valm;

  Counter #(.max('h18), .width(10)) counter_1 (.clk(and_1_out));  // open: clr, load, up, count, D, carry, Q
  Clock clock_1 (.out(clock_1_out));
  and and_1 (and_1_out, clock_1_out, ~fetch_1_notvalid);  // AND_Gate
  Fetch fetch_1 (
    .clk(and_1_out), .PC(pcupdate_1_newpc), .valP(fetch_1_valp), .notValid(fetch_1_notvalid),
    .ifun(fetch_1_ifun), .testPC(out_17), .icode(out_1), .rA(fetch_1_ra), .rB(fetch_1_rb), .valC(fetch_1_valc));
  Memory memory_1 (
    .ValE(execute_1_vale), .valA(decode_1_vala), .icode(out_1), .valP(fetch_1_valp), .clk(and_1_out),
    .valM(memory_1_valm));
  Execute execute_1 (
    .icode(out_1), .ifun(fetch_1_ifun), .ValA(decode_1_vala), .ValB(decode_1_valb), .ValC(fetch_1_valc),
    .clk(and_1_out), .ValE(execute_1_vale), .ccOUTPUT(out_2), .setflag(out_3),
    .CondSignal(execute_1_condsignal));  // open: ZF, SF, Overflow
  pcUpdate pcupdate_1 (
    .clk(and_1_out), .valP(fetch_1_valp), .valC(fetch_1_valc), .valM(memory_1_valm), .icode(out_1),
    .cnd(execute_1_condsignal), .newPC(pcupdate_1_newpc));
  Decode decode_1 (
    .clk(and_1_out), .valE(execute_1_vale), .valM(memory_1_valm), .rA(fetch_1_ra), .rB(fetch_1_rb),
    .icode(out_1), .valA(decode_1_vala), .valB(decode_1_valb), .showRAX(showRAX), .showRCX(showRCX),
    .showRDX(showRDX), .showRBX(showRBX), .showRSP(showRSP), .showRBP(showRBP), .showRSI(showRSI),
    .showRDI(showRDI), .showR8(showR8), .showR9(showR9), .showR10(showR10), .showR11(showR11),
    .showR12(showR12), .showR13(showR13), .showR14(showR14));
  // Probe on memory_1_valm
  // Probe on execute_1_vale
endmodule

module instruction_mem (
  input  clk,
  input  [11:0] PC_address,
  output [7:0] byte0,
  output [7:0] byte1,
  output [7:0] byte2,
  output [7:0] byte3,
  output [7:0] byte4,
  output [7:0] byte5,
  output [7:0] byte6,
  output [7:0] byte7,
  output [7:0] byte8,
  output [7:0] byte9
);

  wire decoder_1_out1, decoder_1_out2, decoder_1_out3, decoder_1_out4, decoder_1_out5, decoder_1_out6,
       decoder_1_out7, decoder_1_out8, decoder_1_out9, decoder_1_out10, multiplexer_1_out;
  wire [4:0] counter_1_q;
  wire [7:0] rom_1_data;
  wire [11:0] adder_1_out, count_q, register_1_q;

  Adder #(.width(12)) adder_1 (.a(count_q), .b(PC_address), .out(adder_1_out));  // open: cin, cout
  Register #(.width(12)) register_1 (
    .D(adder_1_out), .en(multiplexer_1_out), .clk(clk), .Q(register_1_q));  // open: clr
  Decoder #(.select(5)) decoder_1 (
    .out1(decoder_1_out1), .out2(decoder_1_out2), .out3(decoder_1_out3), .out4(decoder_1_out4),
    .out5(decoder_1_out5), .out6(decoder_1_out6), .out7(decoder_1_out7), .out8(decoder_1_out8),
    .out9(decoder_1_out9), .out10(decoder_1_out10), .sel(counter_1_q));  // open: out0, out11, out12, out13, out14, out15, out16, out17, out18, out19, out20, out21, out22, out23, out24, out25, out26, out27, out28, out29, out30, out31, en
  ROM #(.addrWidth(12)) rom_1 (.addr(register_1_q), .data(rom_1_data));
  Counter #(.max('h18), .width(5)) counter_1 (.clk(clk), .Q(counter_1_q));  // open: clr, load, up, count, D, carry
  Register byt0 (.D(rom_1_data), .en(decoder_1_out1), .clk(clk), .Q(byte0));  // open: clr
  Register byt1 (.D(rom_1_data), .en(decoder_1_out2), .clk(clk), .Q(byte1));  // open: clr
  Register register_2 (.D(rom_1_data), .en(decoder_1_out3), .clk(clk), .Q(byte2));  // open: clr
  Register register_3 (.D(rom_1_data), .en(decoder_1_out4), .clk(clk), .Q(byte3));  // open: clr
  Register register_4 (.D(rom_1_data), .en(decoder_1_out5), .clk(clk), .Q(byte4));  // open: clr
  Register register_5 (.D(rom_1_data), .en(decoder_1_out6), .clk(clk), .Q(byte5));  // open: clr
  Register register_6 (.D(rom_1_data), .en(decoder_1_out7), .clk(clk), .Q(byte6));  // open: clr
  Register register_7 (.D(rom_1_data), .en(decoder_1_out8), .clk(clk), .Q(byte7));  // open: clr
  Register register_8 (.D(rom_1_data), .en(decoder_1_out9), .clk(clk), .Q(byte8));  // open: clr
  Register register_9 (.D(rom_1_data), .en(decoder_1_out10), .clk(clk), .Q(byte9));  // open: clr
  Multiplexer #(.select(5)) multiplexer_1 (
    .in0(1'b1), .in1(1'b1), .in2(1'b1), .in3(1'b1), .in4(1'b1), .in5(1'b1), .in6(1'b1), .in7(1'b1),
    .in8(1'b1), .in9(1'b1), .in10(1'b0), .in11(1'b0), .in12(1'b0), .in13(1'b0), .in14(1'b0), .in15(1'b0),
    .in16(1'b0), .in17(1'b0), .in18(1'b0), .in19(1'b0), .in20(1'b0), .in21(1'b0), .in22(1'b0), .in23(1'b0),
    .in24(1'b0), .out(multiplexer_1_out), .sel(counter_1_q));  // open: in25, in26, in27, in28, in29, in30, in31
  Counter #(.max('h9), .width(12)) count (
    .clr(1'b0), .up(1'b1), .count(multiplexer_1_out), .clk(clk), .Q(count_q));  // open: load, D, carry

  // Notes on the sheet:
  //   contents of rom_1 (hex, n*v repeats v):
  //   30 f4 0 2 6*0 80 9 1 7*0 30 fb 8 7*0 30 f9 0 3 6*0 30 fa 1 7*0 40 a9 8*0 60 b9 30 fa 34 7*0 40 a9
  //   8*0 60 b9 30 fa 25 7*0 40 a9 8*0 60 b9 30 fa 12 7*0 40 a9 8*0 60 b9 30 fa 22 7*0 40 a9 8*0 60 b9 30
  //   fa 11 7*0 40 a9 8*0 60 b9 30 fa 90 7*0 40 a9 8*0 60 b9 30 fa 14 7*0 40 a9 8*0 60 b9 30 fa 16 7*0 40
  //   a9 8*0 60 b9 30 fa 0 5 6*0 40 a9 8*0 63 aa 63 99 63 bb 90 80 14 7*0 30 f7 0 3 6*0 30 f6 a 7*0 80 30
  //   1 6*0 90 30 f8 8 7*0 30 f9 1 7*0 30 f2 8*0 20 2e 61 9e 61 6e 75 b5 1 6*0 60 92 20 7a 20 7b 60 8b 30
  //   f3 8*0 50 ca 8*0 50 db 8*0 61 cd 75 4e 1 6*0 80 b6 1 6*0 60 8a 60 8b 60 93 20 6e 61 2e 61 3e 76 6f 1
  //   6*0 70 4e 1 6*0 90 50 ca 8*0 50 db 8*0 40 da 8*0 40 cb 8*0 90
  //   24 tick cycle
  //   instruction memory
endmodule

module needRegis (
  input  [3:0] icode,
  output needRegs
);

  wire comparator_1_eq, comparator_2_eq, comparator_3_eq, comparator_4_eq, comparator_5_eq, comparator_6_eq,
       comparator_7_eq;

  Comparator #(.width(4)) comparator_1 (.a(icode), .b(4'b1010), .eq(comparator_1_eq));  // open: gt, lt
  Comparator #(.width(4)) comparator_2 (.a(icode), .b(4'b0010), .eq(comparator_2_eq));  // open: gt, lt
  Comparator #(.width(4)) comparator_3 (.a(icode), .b(4'b0100), .eq(comparator_3_eq));  // open: gt, lt
  Comparator #(.width(4)) comparator_4 (.a(icode), .b(4'b0101), .eq(comparator_4_eq));  // open: gt, lt
  Comparator #(.width(4)) comparator_5 (.a(icode), .b(4'b1011), .eq(comparator_5_eq));  // open: gt, lt
  Comparator #(.width(4)) comparator_6 (.a(icode), .b(4'b0110), .eq(comparator_6_eq));  // open: gt, lt
  Comparator #(.width(4)) comparator_7 (.a(icode), .b(4'b0011), .eq(comparator_7_eq));  // open: gt, lt
  or or_1 (needRegs, comparator_1_eq, comparator_2_eq, comparator_3_eq, comparator_4_eq, comparator_5_eq, comparator_6_eq, comparator_7_eq);
endmodule

module needValC (
  input  [3:0] icode,
  output needC
);

  wire comparator_1_eq, comparator_2_eq, comparator_3_eq, comparator_4_eq, comparator_5_eq;

  Comparator #(.width(4)) comparator_1 (.a(icode), .b(4'b0011), .eq(comparator_1_eq));  // open: gt, lt
  Comparator #(.width(4)) comparator_2 (.a(icode), .b(4'b0100), .eq(comparator_2_eq));  // open: gt, lt
  Comparator #(.width(4)) comparator_3 (.a(icode), .b(4'b0101), .eq(comparator_3_eq));  // open: gt, lt
  Comparator #(.width(4)) comparator_4 (.a(icode), .b(4'b0111), .eq(comparator_4_eq));  // open: gt, lt
  Comparator #(.width(4)) comparator_5 (.a(icode), .b(4'b1000), .eq(comparator_5_eq));  // open: gt, lt
  or or_1 (needC, comparator_1_eq, comparator_2_eq, comparator_3_eq, comparator_4_eq, comparator_5_eq);
endmodule

module InstrValid (
  input  [3:0] icode,
  input  en,
  output not_valid
);

  wire comparator_1_eq, comparator_2_eq, comparator_3_eq, comparator_4_eq, comparator_5_eq, comparator_6_eq,
       comparator_7_eq, comparator_8_eq, comparator_9_eq, comparator_10_eq, not_1_out, or_1_out;

  Comparator #(.width(4)) comparator_1 (.a(icode), .b(4'b0011), .eq(comparator_1_eq));  // open: gt, lt
  Comparator #(.width(4)) comparator_2 (.a(icode), .b(4'b0100), .eq(comparator_2_eq));  // open: gt, lt
  Comparator #(.width(4)) comparator_3 (.a(icode), .b(4'b0101), .eq(comparator_3_eq));  // open: gt, lt
  Comparator #(.width(4)) comparator_4 (.a(icode), .b(4'b0110), .eq(comparator_4_eq));  // open: gt, lt
  Comparator #(.width(4)) comparator_5 (.a(icode), .b(4'b0111), .eq(comparator_5_eq));  // open: gt, lt
  Comparator #(.width(4)) comparator_6 (.a(icode), .b(4'b1000), .eq(comparator_6_eq));  // open: gt, lt
  Comparator #(.width(4)) comparator_7 (.a(icode), .b(4'b1001), .eq(comparator_7_eq));  // open: gt, lt
  Comparator #(.width(4)) comparator_8 (.a(icode), .b(4'b1010), .eq(comparator_8_eq));  // open: gt, lt
  Comparator #(.width(4)) comparator_9 (.a(icode), .b(4'b1011), .eq(comparator_9_eq));  // open: gt, lt
  Comparator #(.width(4)) comparator_10 (.a(icode), .b(4'b0010), .eq(comparator_10_eq));  // open: gt, lt
  or or_1 (or_1_out, comparator_1_eq, comparator_2_eq, comparator_3_eq, comparator_4_eq, comparator_5_eq, comparator_6_eq, comparator_7_eq, comparator_8_eq, comparator_9_eq, comparator_10_eq);
  not not_1 (not_1_out, or_1_out);
  and and_1 (not_valid, not_1_out, en);

  // Notes on the sheet:
  //   rrmovq
endmodule

module byteEnables (
  input  needRegs,
  output e1,
  output e2,
  output e3,
  output e4,
  output e5,
  output e6,
  output e7,
  output e8,
  output e9
);

  not not_1 (e1, needRegs);

  assign e2 = 1'b1;
  assign e3 = 1'b1;
  assign e4 = 1'b1;
  assign e5 = 1'b1;
  assign e6 = 1'b1;
  assign e7 = 1'b1;
  assign e8 = 1'b1;
  assign e9 = needRegs;
endmodule

module PC_Increment (
  input  [11:0] oldPC,
  input  needRegs,
  input  needValC,
  output [11:0] valP
);

  wire and_1_out;
  wire [11:0] adder_1_out, adder_2_out, adder_3_out, multiplexer_1_out;

  and and_1 (and_1_out, needRegs, needValC);
  Adder #(.width(12)) adder_1 (.a(oldPC), .b(12'h2), .out(adder_1_out));  // open: cin, cout
  Adder #(.width(12)) adder_2 (.a(oldPC), .b(12'h9), .out(adder_2_out));  // open: cin, cout
  Adder #(.width(12)) adder_3 (.a(oldPC), .b(12'ha), .out(adder_3_out));  // open: cin, cout
  Multiplexer #(.width(12)) multiplexer_1 (
    .in0(adder_1_out), .in1(adder_2_out), .out(multiplexer_1_out), .sel(needValC));
  Multiplexer #(.width(12)) multiplexer_2 (.in0(multiplexer_1_out), .in1(adder_3_out), .out(valP), .sel(and_1_out));

  // Notes on the sheet:
  //   increment by 2
  //   increment by 9
  //   needs val c?
  //   needs both?
endmodule

module Fetch (
  input  clk,
  input  [11:0] PC,
  output [11:0] valP,
  output notValid,
  output [3:0] ifun,
  output [11:0] testPC,
  output [3:0] icode,
  output [3:0] rA,
  output [3:0] rB,
  output [63:0] valC
);

  wire and_1_out, and_2_out, and_3_out, and_4_out, and_5_out, and_6_out, and_7_out, and_8_out, and_9_out,
       byteenables_1_e1, byteenables_1_e2, byteenables_1_e3, byteenables_1_e4, byteenables_1_e5,
       byteenables_1_e6, byteenables_1_e7, byteenables_1_e8, byteenables_1_e9, counter_1_p2,
       multiplexer_1_out, multiplexer_2_out, needregis_1_needregs, needvalc_1_needc;
  wire [3:0] instruction_mem_1_byte1, instruction_mem_1_byte1_2;
  wire [4:0] counter_1_p4;
  wire [7:0] byte1_q, byte2_q, byte3_q, byte4_q, byte5_q, byte6_q, byte7_q, byte8_q, byte9_q,
       instruction_mem_1_byte2, instruction_mem_1_byte3, instruction_mem_1_byte4, instruction_mem_1_byte5,
       instruction_mem_1_byte6, instruction_mem_1_byte7, instruction_mem_1_byte8, instruction_mem_1_byte9;

  Multiplexer #(.select(5)) multiplexer_1 (
    .in0(1'b0), .in1(1'b0), .in2(1'b0), .in3(1'b1), .in4(1'b1), .in5(1'b1), .in6(1'b1), .in7(1'b1),
    .in8(1'b1), .in9(1'b1), .in10(1'b1), .in11(1'b1), .in12(1'b1), .in13(1'b1), .in14(1'b1), .in15(1'b1),
    .in16(1'b1), .in17(1'b1), .in18(1'b1), .in19(1'b1), .in20(1'b1), .in21(1'b1), .in22(1'b1), .in23(1'b1),
    .in24(1'b1), .in25(1'b1), .out(multiplexer_1_out), .sel(counter_1_p4));  // open: in26, in27, in28, in29, in30, in31
  // Counter #(.max('h18), .width(5)) counter_1: pin names not known; wires that end beside it: clk, counter_1_p2, counter_1_p2, counter_1_p4
  Register #(.width(12)) register_1 (.D(PC), .en(multiplexer_2_out), .clk(clk), .Q(testPC));  // open: clr
  Multiplexer #(.select(5)) multiplexer_2 (
    .in0(1'b0), .in1(1'b0), .in2(1'b0), .in3(1'b0), .in4(1'b0), .in5(1'b0), .in6(1'b0), .in7(1'b0),
    .in8(1'b0), .in9(1'b0), .in10(1'b0), .in11(1'b0), .in12(1'b0), .in13(1'b0), .in14(1'b0), .in15(1'b0),
    .in16(1'b0), .in17(1'b0), .in18(1'b0), .in19(1'b0), .in20(1'b0), .in21(1'b0), .in22(1'b0), .in23(1'b0),
    .in24(1'b1), .out(multiplexer_2_out), .sel(counter_1_p4));  // open: in25, in26, in27, in28, in29, in30, in31
  instruction_mem instruction_mem_1 (
    .clk(clk), .PC_address(testPC), .byte0({icode, ifun}),
    .byte1({instruction_mem_1_byte1_2, instruction_mem_1_byte1}), .byte2(instruction_mem_1_byte2),
    .byte3(instruction_mem_1_byte3), .byte4(instruction_mem_1_byte4), .byte5(instruction_mem_1_byte5),
    .byte6(instruction_mem_1_byte6), .byte7(instruction_mem_1_byte7), .byte8(instruction_mem_1_byte8),
    .byte9(instruction_mem_1_byte9));
  InstrValid instrvalid_1 (.icode(icode), .en(multiplexer_1_out), .not_valid(notValid));
  needRegis needregis_1 (.icode(icode), .needRegs(needregis_1_needregs));
  needValC needvalc_1 (.icode(icode), .needC(needvalc_1_needc));
  Register #(.width(4)) register_2 (
    .D(instruction_mem_1_byte1_2), .en(needregis_1_needregs), .clk(clk), .Q(rA));  // open: clr
  Register #(.width(4)) register_3 (
    .D(instruction_mem_1_byte1), .en(needregis_1_needregs), .clk(clk), .Q(rB));  // open: clr
  byteEnables byteenables_1 (
    .needRegs(needregis_1_needregs), .e1(byteenables_1_e1), .e2(byteenables_1_e2), .e3(byteenables_1_e3),
    .e4(byteenables_1_e4), .e5(byteenables_1_e5), .e6(byteenables_1_e6), .e7(byteenables_1_e7),
    .e8(byteenables_1_e8), .e9(byteenables_1_e9));
  and and_1 (and_1_out, needvalc_1_needc, byteenables_1_e1);
  and and_2 (and_2_out, needvalc_1_needc, byteenables_1_e2);
  and and_3 (and_3_out, needvalc_1_needc, byteenables_1_e3);
  and and_4 (and_4_out, needvalc_1_needc, byteenables_1_e4);
  and and_5 (and_5_out, needvalc_1_needc, byteenables_1_e5);
  and and_6 (and_6_out, needvalc_1_needc, byteenables_1_e6);
  and and_7 (and_7_out, needvalc_1_needc, byteenables_1_e7);
  and and_8 (and_8_out, needvalc_1_needc, byteenables_1_e8);
  and and_9 (and_9_out, needvalc_1_needc, byteenables_1_e9);
  Register byte1 (
    .D({instruction_mem_1_byte1_2, instruction_mem_1_byte1}), .en(and_1_out), .clk(clk), .Q(byte1_q));  // open: clr
  Register byte2 (.D(instruction_mem_1_byte2), .en(and_2_out), .clk(clk), .Q(byte2_q));  // open: clr
  Register byte3 (.D(instruction_mem_1_byte3), .en(and_3_out), .clk(clk), .Q(byte3_q));  // open: clr
  Register byte4 (.D(instruction_mem_1_byte4), .en(and_4_out), .clk(clk), .Q(byte4_q));  // open: clr
  Register byte5 (.D(instruction_mem_1_byte5), .en(and_5_out), .clk(clk), .Q(byte5_q));  // open: clr
  PC_Increment pc_increment_1 (
    .oldPC(testPC), .needRegs(needregis_1_needregs), .needValC(needvalc_1_needc), .valP(valP));
  Register byte6 (.D(instruction_mem_1_byte6), .en(and_6_out), .clk(clk), .Q(byte6_q));  // open: clr
  Register byte7 (.D(instruction_mem_1_byte7), .en(and_7_out), .clk(clk), .Q(byte7_q));  // open: clr
  Register byte8 (.D(instruction_mem_1_byte8), .en(and_8_out), .clk(clk), .Q(byte8_q));  // open: clr
  Register byte9 (.D(instruction_mem_1_byte9), .en(and_9_out), .clk(clk), .Q(byte9_q));  // open: clr
  Multiplexer #(.width(64)) multiplexer_3 (
    .in0({byte9_q, byte8_q, byte7_q, byte6_q, byte5_q, byte4_q, byte3_q, byte2_q}),
    .in1({byte8_q, byte7_q, byte6_q, byte5_q, byte4_q, byte3_q, byte2_q, byte1_q}), .out(valC),
    .sel(byteenables_1_e1));

  // Notes on the sheet:
  //   icode
  //   w byte 9
  //   w byte 1
endmodule

module Decode (
  input  clk,
  input  [63:0] valE,
  input  [63:0] valM,
  input  [3:0] rA,
  input  [3:0] rB,
  input  [3:0] icode,
  output [63:0] valA,
  output [63:0] valB,
  output [63:0] showRAX,
  output [63:0] showRCX,
  output [63:0] showRDX,
  output [63:0] showRBX,
  output [63:0] showRSP,
  output [63:0] showRBP,
  output [63:0] showRSI,
  output [63:0] showRDI,
  output [63:0] showR8,
  output [63:0] showR9,
  output [63:0] showR10,
  output [63:0] showR11,
  output [63:0] showR12,
  output [63:0] showR13,
  output [63:0] showR14
);

  wire multiplexer_1_out;
  wire [3:0] dste_1_deste, dstm_1_out_4, srca_1_sourcea, srcb_1_out_4;
  wire [4:0] counter_1_q;

  Counter #(.max('h18), .width(5)) counter_1 (.clk(clk), .Q(counter_1_q));  // open: clr, load, up, count, D, carry
  Multiplexer #(.select(5)) multiplexer_1 (
    .in0(1'b0), .in1(1'b0), .in2(1'b0), .in3(1'b0), .in4(1'b0), .in5(1'b0), .in6(1'b0), .in7(1'b0),
    .in8(1'b0), .in9(1'b0), .in10(1'b0), .in11(1'b1), .in12(1'b1), .in13(1'b1), .in14(1'b1), .in15(1'b1),
    .in16(1'b1), .in17(1'b1), .in18(1'b1), .in19(1'b1), .in20(1'b1), .in21(1'b1), .in22(1'b1), .in23(1'b1),
    .in24(1'b1), .out(multiplexer_1_out), .sel(counter_1_q));  // open: in25, in26, in27, in28, in29, in30, in31
  srcA srca_1 (.rA(rA), .icode(icode), .en(multiplexer_1_out), .sourceA(srca_1_sourcea));
  dstE dste_1 (.rB(rB), .icode(icode), .en(multiplexer_1_out), .destE(dste_1_deste));
  dstM dstm_1 (.en(multiplexer_1_out), .iCode(icode), .rA(rA), .out_4(dstm_1_out_4));
  srcB srcb_1 (.rB(rB), .en(multiplexer_1_out), .icode(icode), .out_4(srcb_1_out_4));
  Register_File register_file_1 (
    .clk(clk), .valE(valE), .valM(valM), .srcA(srca_1_sourcea), .dstE(dste_1_deste), .icode(icode),
    .dstM(dstm_1_out_4), .srcB(srcb_1_out_4), .valA(valA), .valB(valB), .showRAX(showRAX), .showRCX(showRCX),
    .showRDX(showRDX), .showRBX(showRBX), .showRSP(showRSP), .showRBP(showRBP), .showRSI(showRSI),
    .showRDI(showRDI), .showR8(showR8), .showR9(showR9), .showR10(showR10), .showR11(showR11),
    .showR12(showR12), .showR13(showR13), .showR14(showR14));

  // Notes on the sheet:
  //   needed for WB
  //   decode and
  //   WB enable
endmodule

module srcA (
  input  [3:0] rA,
  input  [3:0] icode,
  input  en,
  output [3:0] sourceA
);

  Multiplexer #(.enable("true"), .select(4), .width(4)) multiplexer_1 (
    .in0(4'b1111), .in1(4'b1111), .in2(rA), .in3(4'b1111), .in4(rA), .in5(rA), .in6(rA), .in7(4'b1111),
    .in8(4'b1111), .in9(4'b0100), .in10(rA), .in11(4'b0100), .out(sourceA), .sel(icode), .en(en));  // open: in12, in13, in14, in15

  // Notes on the sheet:
  //   rsp
endmodule

module dstE (
  input  [3:0] rB,
  input  [3:0] icode,
  input  en,
  output [3:0] destE
);

  Multiplexer #(.enable("true"), .select(4), .width(4)) multiplexer_1 (
    .in0(4'b1111), .in1(4'b1111), .in2(rB), .in3(rB), .in4(4'b1111), .in5(4'b1111), .in6(rB), .in7(4'b1111),
    .in8(4'b0100), .in9(4'b0100), .in10(4'b0100), .in11(4'b0100), .out(destE), .sel(icode), .en(en));  // open: in12, in13, in14, in15

  // Notes on the sheet:
  //   rsp
endmodule

module Register_File (
  input  clk,
  input  [63:0] valE,
  input  [63:0] valM,
  input  [3:0] srcA,
  input  [3:0] dstE,
  input  [3:0] icode,
  input  [3:0] dstM,
  input  [3:0] srcB,
  output [63:0] valA,
  output [63:0] valB,
  output [63:0] showRAX,
  output [63:0] showRCX,
  output [63:0] showRDX,
  output [63:0] showRBX,
  output [63:0] showRSP,
  output [63:0] showRBP,
  output [63:0] showRSI,
  output [63:0] showRDI,
  output [63:0] showR8,
  output [63:0] showR9,
  output [63:0] showR10,
  output [63:0] showR11,
  output [63:0] showR12,
  output [63:0] showR13,
  output [63:0] showR14
);

  wire demultiplexer_2_out0, demultiplexer_2_out1, demultiplexer_2_out2, demultiplexer_2_out3,
       demultiplexer_2_out4, demultiplexer_2_out5, demultiplexer_2_out6, demultiplexer_2_out7,
       demultiplexer_2_out8, demultiplexer_2_out9, demultiplexer_2_out10, demultiplexer_2_out11,
       demultiplexer_2_out12, demultiplexer_2_out13, demultiplexer_2_out14, demultiplexer_2_out15,
       multiplexer_1_out, multiplexer_2_out, multiplexer_5_out, multiplexer_9_out, or_1_out;
  wire [3:0] multiplexer_3_out;
  wire [4:0] counter_2_q;
  wire [7:0] counter_1_q;
  wire [63:0] demultiplexer_1_out0, demultiplexer_1_out1, demultiplexer_1_out2, demultiplexer_1_out3,
       demultiplexer_1_out4, demultiplexer_1_out5, demultiplexer_1_out6, demultiplexer_1_out7,
       demultiplexer_1_out8, demultiplexer_1_out9, demultiplexer_1_out10, demultiplexer_1_out11,
       demultiplexer_1_out12, demultiplexer_1_out13, demultiplexer_1_out14, demultiplexer_1_out15,
       multiplexer_4_out, multiplexer_6_out, no_register_q;

  Counter #(.max('h18)) counter_1 (.clk(clk), .Q(counter_1_q));  // open: clr, load, up, count, D, carry
  Multiplexer #(.enable("true"), .select(4)) multiplexer_1 (
    .in0(1'b0), .in1(1'b0), .in2(1'b0), .in3(1'b0), .in4(1'b0), .in5(1'b1), .in6(1'b0), .in7(1'b0),
    .in8(1'b0), .in9(1'b0), .in10(1'b0), .in11(1'b1), .out(multiplexer_1_out), .sel(icode),
    .en(multiplexer_2_out));  // open: in12, in13, in14, in15
  Multiplexer #(.select(5)) multiplexer_2 (
    .in0(1'b0), .in1(1'b0), .in2(1'b0), .in3(1'b0), .in4(1'b0), .in5(1'b0), .in6(1'b0), .in7(1'b0),
    .in8(1'b0), .in9(1'b0), .in10(1'b0), .in11(1'b0), .in12(1'b0), .in13(1'b0), .in14(1'b0), .in15(1'b0),
    .in16(1'b0), .in17(1'b0), .in18(1'b0), .in19(1'b0), .in20(1'b0), .in21(1'b0), .in22(1'b0), .in23(1'b0),
    .in24(1'b1), .in25(1'b0), .in26(1'b0), .in27(1'b0), .in28(1'b0), .in29(1'b0), .in30(1'b0), .in31(1'b0),
    .out(multiplexer_2_out), .sel(counter_1_q[4:0]));
  Multiplexer #(.enable("true"), .width(4)) multiplexer_3 (
    .in0(dstE), .in1(dstM), .out(multiplexer_3_out), .sel(multiplexer_1_out), .en(multiplexer_2_out));
  Multiplexer #(.enable("true"), .width(64)) multiplexer_4 (
    .in0(valE), .in1(valM), .out(multiplexer_4_out), .sel(multiplexer_1_out), .en(multiplexer_2_out));
  Multiplexer #(.enable("true"), .select(4)) multiplexer_5 (
    .in0(1'b0), .in1(1'b0), .in2(1'b0), .in3(1'b0), .in4(1'b0), .in5(1'b0), .in6(1'b0), .in7(1'b0),
    .in8(1'b0), .in9(1'b0), .in10(1'b0), .in11(1'b1), .out(multiplexer_5_out), .sel(icode),
    .en(multiplexer_2_out));  // open: in12, in13, in14, in15
  Demultiplexer #(.enable("true"), .select(4), .width(64)) demultiplexer_1 (
    .out0(demultiplexer_1_out0), .out1(demultiplexer_1_out1), .out2(demultiplexer_1_out2),
    .out3(demultiplexer_1_out3), .out4(demultiplexer_1_out4), .out5(demultiplexer_1_out5),
    .out6(demultiplexer_1_out6), .out7(demultiplexer_1_out7), .out8(demultiplexer_1_out8),
    .out9(demultiplexer_1_out9), .out10(demultiplexer_1_out10), .out11(demultiplexer_1_out11),
    .out12(demultiplexer_1_out12), .out13(demultiplexer_1_out13), .out14(demultiplexer_1_out14),
    .out15(demultiplexer_1_out15), .in(multiplexer_4_out), .sel(multiplexer_3_out), .en(multiplexer_2_out));
  Demultiplexer #(.select(4)) demultiplexer_2 (
    .out0(demultiplexer_2_out0), .out1(demultiplexer_2_out1), .out2(demultiplexer_2_out2),
    .out3(demultiplexer_2_out3), .out4(demultiplexer_2_out4), .out5(demultiplexer_2_out5),
    .out6(demultiplexer_2_out6), .out7(demultiplexer_2_out7), .out8(demultiplexer_2_out8),
    .out9(demultiplexer_2_out9), .out10(demultiplexer_2_out10), .out11(demultiplexer_2_out11),
    .out12(demultiplexer_2_out12), .out13(demultiplexer_2_out13), .out14(demultiplexer_2_out14),
    .out15(demultiplexer_2_out15), .in(multiplexer_2_out), .sel(multiplexer_3_out));
  Multiplexer #(.width(64)) multiplexer_6 (
    .in0(demultiplexer_1_out4), .in1(valE), .out(multiplexer_6_out), .sel(multiplexer_5_out));
  or or_1 (or_1_out, demultiplexer_2_out4, multiplexer_5_out);
  Register #(.width(64)) rax (
    .D(demultiplexer_1_out0), .en(demultiplexer_2_out0), .clk(clk), .Q(showRAX));  // open: clr
  Register #(.width(64)) rcx (
    .D(demultiplexer_1_out1), .en(demultiplexer_2_out1), .clk(clk), .Q(showRCX));  // open: clr
  Register #(.width(64)) rdx (
    .D(demultiplexer_1_out2), .en(demultiplexer_2_out2), .clk(clk), .Q(showRDX));  // open: clr
  Register #(.width(64)) rbx (
    .D(demultiplexer_1_out3), .en(demultiplexer_2_out3), .clk(clk), .Q(showRBX));  // open: clr
  Register #(.width(64)) rsp (.D(multiplexer_6_out), .en(or_1_out), .clk(clk), .Q(showRSP));  // open: clr
  Register #(.width(64)) rbp (
    .D(demultiplexer_1_out5), .en(demultiplexer_2_out5), .clk(clk), .Q(showRBP));  // open: clr
  Register #(.width(64)) rsi (
    .D(demultiplexer_1_out6), .en(demultiplexer_2_out6), .clk(clk), .Q(showRSI));  // open: clr
  Register #(.width(64)) rdi (
    .D(demultiplexer_1_out7), .en(demultiplexer_2_out7), .clk(clk), .Q(showRDI));  // open: clr
  Register #(.width(64)) r8 (.D(demultiplexer_1_out8), .en(demultiplexer_2_out8), .clk(clk), .Q(showR8));  // open: clr
  Register #(.width(64)) r9 (.D(demultiplexer_1_out9), .en(demultiplexer_2_out9), .clk(clk), .Q(showR9));  // open: clr
  Register #(.width(64)) r10 (
    .D(demultiplexer_1_out10), .en(demultiplexer_2_out10), .clk(clk), .Q(showR10));  // open: clr
  Register #(.width(64)) r11 (
    .D(demultiplexer_1_out11), .en(demultiplexer_2_out11), .clk(clk), .Q(showR11));  // open: clr
  Register #(.width(64)) r12 (
    .D(demultiplexer_1_out12), .en(demultiplexer_2_out12), .clk(clk), .Q(showR12));  // open: clr
  Register #(.width(64)) r13 (
    .D(demultiplexer_1_out13), .en(demultiplexer_2_out13), .clk(clk), .Q(showR13));  // open: clr
  Register #(.width(64)) r14 (
    .D(demultiplexer_1_out14), .en(demultiplexer_2_out14), .clk(clk), .Q(showR14));  // open: clr
  Register #(.width(64)) no_register (
    .D(demultiplexer_1_out15), .en(demultiplexer_2_out15), .clk(clk), .Q(no_register_q));  // open: clr
  Counter #(.max('h18), .width(5)) counter_2 (.clk(clk), .Q(counter_2_q));  // open: clr, load, up, count, D, carry
  Multiplexer #(.enable("true"), .select(4), .width(64)) multiplexer_7 (
    .in0(showRAX), .in1(showRCX), .in2(showRDX), .in3(showRBX), .in4(showRSP), .in5(showRBP), .in6(showRSI),
    .in7(showRDI), .in8(showR8), .in9(showR9), .in10(showR10), .in11(showR11), .in12(showR12),
    .in13(showR13), .in14(showR14), .in15(no_register_q), .out(valA), .sel(srcA), .en(multiplexer_9_out));
  Multiplexer #(.enable("true"), .select(4), .width(64)) multiplexer_8 (
    .in0(showRAX), .in1(showRCX), .in2(showRDX), .in3(showRBX), .in4(showRSP), .in5(showRBP), .in6(showRSI),
    .in7(showRDI), .in8(showR8), .in9(showR9), .in10(showR10), .in11(showR11), .in12(showR12),
    .in13(showR13), .in14(showR14), .in15(no_register_q), .out(valB), .sel(srcB), .en(multiplexer_9_out));
  Multiplexer #(.select(5)) multiplexer_9 (
    .in0(1'b0), .in1(1'b0), .in2(1'b0), .in3(1'b0), .in4(1'b0), .in5(1'b0), .in6(1'b0), .in7(1'b0),
    .in8(1'b0), .in9(1'b0), .in10(1'b0), .in11(1'b1), .in12(1'b1), .in13(1'b1), .in14(1'b1), .in15(1'b1),
    .in16(1'b1), .in17(1'b1), .in18(1'b1), .in19(1'b1), .in20(1'b1), .in21(1'b1), .in22(1'b1), .in23(1'b1),
    .in24(1'b1), .out(multiplexer_9_out), .sel(counter_2_q));  // open: in25, in26, in27, in28, in29, in30, in31

  // Notes on the sheet:
  //   M is 1 
  //   2 if 15
  //   if is f
  //   using M
  //   write enable
  //   show registers for testing
  //   en
endmodule

module dstM (
  input  en,
  input  [3:0] iCode,
  input  [3:0] rA,
  output [3:0] out_4
);

  wire decoder_1_out5, decoder_1_out11, or_1_out;

  Decoder #(.select(4)) decoder_1 (
    .out5(decoder_1_out5), .out11(decoder_1_out11), .sel(iCode), .en(en));  // open: out0, out1, out2, out3, out4, out6, out7, out8, out9, out10, out12, out13, out14, out15
  or or_1 (or_1_out, decoder_1_out5, decoder_1_out11);
  Multiplexer #(.enable("true"), .width(4)) multiplexer_1 (
    .in0(4'b1111), .in1(rA), .out(out_4), .sel(or_1_out), .en(en));
endmodule

module srcB (
  input  [3:0] rB,
  input  en,
  input  [3:0] icode,
  output [3:0] out_4
);

  wire decoder_1_out4, decoder_1_out5, decoder_1_out6, decoder_1_out8, decoder_1_out9, decoder_1_out10,
       decoder_1_out11, or_1_out, or_2_out;
  wire [3:0] multiplexer_1_out;

  Multiplexer #(.width(4)) multiplexer_1 (.in0(4'b1111), .in1(rB), .out(multiplexer_1_out), .sel(or_1_out));
  Decoder #(.select(4)) decoder_1 (
    .out4(decoder_1_out4), .out5(decoder_1_out5), .out6(decoder_1_out6), .out8(decoder_1_out8),
    .out9(decoder_1_out9), .out10(decoder_1_out10), .out11(decoder_1_out11), .sel(icode), .en(en));  // open: out0, out1, out2, out3, out7, out12, out13, out14, out15
  or or_1 (or_1_out, decoder_1_out4, decoder_1_out5, decoder_1_out6);
  or or_2 (or_2_out, decoder_1_out8, decoder_1_out9, decoder_1_out10, decoder_1_out11);
  Multiplexer #(.enable("true"), .width(4)) multiplexer_2 (
    .in0(multiplexer_1_out), .in1(4'b0100), .out(out_4), .sel(or_2_out), .en(en));
endmodule

module ALU (
  input  [63:0] A,
  input  clk,
  input  en,
  input  [63:0] B,
  input  [1:0] fun,
  input  [3:0] icode,
  output [63:0] ValE,
  output [2:0] CondCode,
  output ZF,
  output SF,
  output Overflow
);

  wire and_2_out, and_3_out, and_4_out, and_5_out, and_6_out, and_7_out, controlled_buffer_1_out, not_1_out,
       not_2_out, not_3_out, not_4_out, not_5_out, not_6_out, not_7_out, or_1_out, or_2_out, or_3_out;
  wire [1:0] multiplexer_1_out;
  wire [63:0] adder_1_out, and_1_out, subtractor_1_out, xor_1_out;

  Adder #(.width(64)) adder_1 (.a(A), .b(B), .out(adder_1_out));  // open: cin, cout
  Subtractor #(.width(64)) subtractor_1 (.a(B), .b(A), .out(subtractor_1_out));  // open: bin, bout
  assign and_1_out = A & B;  // AND_Gate and_1, 64 bits wide
  assign xor_1_out = A ^ B;  // XOR_Gate xor_1, 64 bits wide
  Multiplexer #(.select(4), .width(2)) multiplexer_1 (
    .in0(2'b00), .in1(2'b00), .in2(2'b00), .in3(2'b00), .in4(2'b00), .in5(2'b00), .in6(fun), .in7(2'b00),
    .in8(2'b01), .in9(2'b00), .in10(2'b01), .in11(2'b00), .in12(2'b00), .in13(2'b00), .in14(2'b00),
    .in15(2'b00), .out(multiplexer_1_out), .sel(icode));
  Multiplexer #(.select(2), .width(64)) multiplexer_2 (
    .in0(adder_1_out), .in1(subtractor_1_out), .in2(and_1_out), .in3(xor_1_out), .out(ValE),
    .sel(multiplexer_1_out));
  not not_1 (not_1_out, multiplexer_1_out[0]);
  not not_2 (not_2_out, multiplexer_1_out[1]);
  not not_3 (not_3_out, ValE[63]);
  not not_4 (not_4_out, ValE[63]);
  not not_5 (not_5_out, A[63]);
  not not_6 (not_6_out, B[63]);
  Comparator #(.width(64)) comparator_1 (.a(ValE), .b({64{1'b0}}), .eq(ZF), .lt(SF));  // open: gt
  and and_2 (and_2_out, not_1_out, not_2_out);
  and and_3 (and_3_out, multiplexer_1_out[0], not_2_out);
  not not_7 (not_7_out, B[63]);
  and and_4 (and_4_out, A[63], B[63], not_4_out);
  and and_5 (and_5_out, not_5_out, not_6_out, ValE[63]);
  and and_6 (and_6_out, not_5_out, B[63], not_3_out);
  and and_7 (and_7_out, not_7_out, A[63], ValE[63]);
  or or_1 (or_1_out, and_6_out, and_7_out);
  or or_2 (or_2_out, and_4_out, and_5_out);
  assign controlled_buffer_1_out = and_3_out ? or_1_out : 1'bz;  // Controlled_Buffer controlled_buffer_1
  assign controlled_buffer_1_out = and_2_out ? or_2_out : 1'bz;  // Controlled_Buffer controlled_buffer_2
  Register #(.width(3)) register_1 (.D({Overflow, SF, ZF}), .en(en), .clk(clk), .Q(CondCode));  // open: clr
  or or_3 (or_3_out, and_3_out, and_2_out);
  Multiplexer multiplexer_3 (.in0(1'b0), .in1(controlled_buffer_1_out), .out(Overflow), .sel(or_3_out));

  // Notes on the sheet:
  //   A
  //   get first bit
  //   (a<0 == b<0) && (t<0 != a<0)
endmodule

module ALUfun (
  input  [3:0] icode,
  input  [3:0] ifun,
  output [1:0] fun
);

  wire and_1_out, not_1_out, not_2_out, not_3_out;

  not not_1 (not_1_out, icode[0]);
  not not_2 (not_2_out, icode[3]);
  and and_1 (and_1_out, not_1_out, icode[1], icode[2], not_2_out);
  assign fun = and_1_out ? ifun[1:0] : 2'bz;  // Controlled_Buffer controlled_buffer_1
  not not_3 (not_3_out, and_1_out);
  assign fun = not_3_out ? 2'b00 : 2'bz;  // Controlled_Buffer controlled_buffer_2

  // Notes on the sheet:
  //   icode must be 6 (OPq)
  //   OP (0,1,2,3)
endmodule

module ALU_A (
  input  en,
  input  [3:0] icode,
  input  [63:0] valA,
  input  [63:0] valC,
  output [63:0] A
);

  Multiplexer #(.enable("true"), .select(4), .width(64)) multiplexer_1 (
    .in2(valA), .in3(valC), .in4(valC), .in5(valC), .in6(valA), .in7({64{1'b0}}), .in8(64'h8), .in9(64'h8),
    .in10(64'h8), .in11(64'h8), .out(A), .sel(icode), .en(en));  // open: in0, in1, in12, in13, in14, in15
endmodule

module ALU_B (
  input  [3:0] icode,
  input  en,
  input  [63:0] ValB,
  output [63:0] B
);

  wire decoder_1_out4, decoder_1_out5, decoder_1_out6, decoder_1_out8, decoder_1_out9, decoder_1_out10,
       decoder_1_out11, not_1_out, or_1_out;

  Decoder #(.select(4)) decoder_1 (
    .out4(decoder_1_out4), .out5(decoder_1_out5), .out6(decoder_1_out6), .out8(decoder_1_out8),
    .out9(decoder_1_out9), .out10(decoder_1_out10), .out11(decoder_1_out11), .sel(icode), .en(en));  // open: out0, out1, out2, out3, out7, out12, out13, out14, out15
  or or_1 (or_1_out, decoder_1_out4, decoder_1_out5, decoder_1_out6, decoder_1_out8, decoder_1_out9, decoder_1_out10, decoder_1_out11);
  not not_1 (not_1_out, or_1_out);
  Multiplexer #(.enable("true"), .width(64)) multiplexer_1 (
    .in0(ValB), .in1({64{1'b0}}), .out(B), .sel(not_1_out), .en(en));
endmodule

module SetCC (
  input  [3:0] icode,
  output set
);

  wire not_1_out, not_2_out, not_3_out;

  not not_1 (not_1_out, icode[0]);
  not not_2 (not_2_out, icode[3]);
  not not_3 (not_3_out, icode[3]);
  and and_1 (set, not_1_out, icode[1], icode[2], not_2_out);
endmodule

module CC (
  input  [2:0] CondCode,
  input  set,
  input  clk,
  output [2:0] CC_output
);

  Register #(.width(3)) register_1 (.D(CondCode), .en(set), .clk(clk), .Q(CC_output));  // open: clr
endmodule

module Cond (
  input  [2:0] CC_output,
  input  [3:0] ifun,
  output condSignal
);

  wire and_1_out, and_2_out, and_3_out, and_4_out, and_5_out, and_6_out, and_7_out, and_8_out, and_9_out,
       decoder_1_out0, decoder_1_out1, decoder_1_out2, decoder_1_out3, decoder_1_out4, decoder_1_out5,
       decoder_1_out6, not_1_out, not_2_out, not_3_out, or_1_out;

  Decoder #(.select(4)) decoder_1 (
    .out0(decoder_1_out0), .out1(decoder_1_out1), .out2(decoder_1_out2), .out3(decoder_1_out3),
    .out4(decoder_1_out4), .out5(decoder_1_out5), .out6(decoder_1_out6), .sel(ifun));  // open: out7, out8, out9, out10, out11, out12, out13, out14, out15, en
  and and_1 (and_1_out, CC_output[2], CC_output[1]);
  and and_2 (and_2_out, CC_output[0], decoder_1_out1);
  and and_3 (and_3_out, decoder_1_out1, and_1_out);
  and and_4 (and_4_out, decoder_1_out2, and_1_out);
  and and_5 (and_5_out, decoder_1_out3, CC_output[0]);
  not not_1 (not_1_out, CC_output[0]);
  and and_6 (and_6_out, CC_output[2], CC_output[1]);
  or or_1 (or_1_out, and_2_out, and_3_out);
  and and_7 (and_7_out, decoder_1_out4, not_1_out);
  and and_8 (and_8_out, decoder_1_out5, not_2_out);
  not not_2 (not_2_out, and_6_out);
  not not_3 (not_3_out, CC_output[0]);
  and and_9 (and_9_out, not_2_out, decoder_1_out6, not_3_out);
  or or_2 (condSignal, decoder_1_out0, or_1_out, and_4_out, and_5_out, and_7_out, and_8_out, and_9_out);
endmodule

module Execute (
  input  [3:0] icode,
  input  [3:0] ifun,
  input  [63:0] ValA,
  input  [63:0] ValB,
  input  [63:0] ValC,
  input  clk,
  output [63:0] ValE,
  output ZF,
  output SF,
  output Overflow,
  output [2:0] ccOUTPUT,
  output setflag,
  output CondSignal
);

  wire multiplexer_1_out;
  wire [1:0] alufun_1_fun;
  wire [2:0] alu_1_condcode;
  wire [4:0] counter_1_q;
  wire [63:0] alu_1_vale, alu_a_1_a, alu_b_1_b;

  Counter #(.max('h18), .width(5)) counter_1 (.clk(clk), .Q(counter_1_q));  // open: clr, load, up, count, D, carry
  Multiplexer #(.select(5)) multiplexer_1 (
    .in0(1'b0), .in1(1'b0), .in2(1'b0), .in3(1'b0), .in4(1'b0), .in5(1'b0), .in6(1'b0), .in7(1'b0),
    .in8(1'b0), .in9(1'b0), .in10(1'b0), .in11(1'b0), .in12(1'b0), .in13(1'b0), .in14(1'b1), .in15(1'b1),
    .in16(1'b1), .in17(1'b1), .in18(1'b1), .in19(1'b1), .in20(1'b1), .in21(1'b1), .in22(1'b1), .in23(1'b1),
    .in24(1'b0), .out(multiplexer_1_out), .sel(counter_1_q));  // open: in25, in26, in27, in28, in29, in30, in31
  ALUfun alufun_1 (.icode(icode), .ifun(ifun), .fun(alufun_1_fun));
  ALU_A alu_a_1 (.en(multiplexer_1_out), .icode(icode), .valA(ValA), .valC(ValC), .A(alu_a_1_a));
  ALU_B alu_b_1 (.icode(icode), .en(multiplexer_1_out), .ValB(ValB), .B(alu_b_1_b));
  SetCC setcc_1 (.icode(icode), .set(setflag));
  ALU alu_1 (
    .A(alu_a_1_a), .clk(clk), .en(multiplexer_1_out), .B(alu_b_1_b), .fun(alufun_1_fun), .icode(icode),
    .ValE(alu_1_vale), .CondCode(alu_1_condcode), .ZF(ZF), .SF(SF), .Overflow(Overflow));
  CC cc_1 (.CondCode(alu_1_condcode), .set(setflag), .clk(clk), .CC_output(ccOUTPUT));
  Register #(.width(64)) register_1 (.D(alu_1_vale), .en(multiplexer_1_out), .clk(clk), .Q(ValE));  // open: clr
  Cond cond_1 (.CC_output(ccOUTPUT), .ifun(ifun), .condSignal(CondSignal));

  // Notes on the sheet:
  //   val_e_en
  //   1 cycle
  //   exec enable
  //   1 cycle
endmodule

module Memory (
  input  [63:0] ValE,
  input  [63:0] valA,
  input  [3:0] icode,
  input  [11:0] valP,
  input  clk,
  output [63:0] valM
);

  wire and_1_out, and_2_out, decoder_1_out0, decoder_1_out1, decoder_1_out2, decoder_1_out3, decoder_1_out4,
       decoder_1_out5, decoder_1_out6, decoder_1_out7, mem_r_w_en_1_r_enable, mem_r_w_en_1_w_enable,
       multiplexer_1_out, multiplexer_2_out, multiplexer_3_out, multiplexer_5_out;
  wire [3:0] counter_3_q, counter_4_q;
  wire [4:0] counter_1_q, counter_2_q;
  wire [7:0] multiplexer_4_out, ram_1_dout, register_1_q, register_2_q, register_3_q, register_4_q,
       register_5_q, register_6_q, register_7_q, register_8_q;
  wire [11:0] memaddr_1_addr;
  wire [63:0] memdata_1_mem;

  Counter #(.max('h18), .width(5)) counter_1 (.clk(clk), .Q(counter_1_q));  // open: clr, load, up, count, D, carry
  Multiplexer #(.select(5)) multiplexer_1 (
    .in0(1'b0), .in1(1'b0), .in2(1'b0), .in3(1'b0), .in4(1'b0), .in5(1'b0), .in6(1'b0), .in7(1'b0),
    .in8(1'b0), .in9(1'b0), .in10(1'b0), .in11(1'b0), .in12(1'b0), .in13(1'b0), .in14(1'b0), .in15(1'b1),
    .in16(1'b1), .in17(1'b1), .in18(1'b1), .in19(1'b1), .in20(1'b1), .in21(1'b1), .in22(1'b1), .in23(1'b0),
    .in24(1'b0), .out(multiplexer_1_out), .sel(counter_1_q));  // open: in25, in26, in27, in28, in29, in30, in31
  Multiplexer #(.select(5)) multiplexer_2 (
    .in0(1'b0), .in1(1'b0), .in2(1'b0), .in3(1'b0), .in4(1'b0), .in5(1'b0), .in6(1'b0), .in7(1'b0),
    .in8(1'b0), .in9(1'b0), .in10(1'b0), .in11(1'b0), .in12(1'b0), .in13(1'b0), .in14(1'b0), .in15(1'b0),
    .in16(1'b1), .in17(1'b1), .in18(1'b1), .in19(1'b1), .in20(1'b1), .in21(1'b1), .in22(1'b1), .in23(1'b1),
    .in24(1'b0), .out(multiplexer_2_out), .sel(counter_1_q));  // open: in25, in26, in27, in28, in29, in30, in31
  mem_r_w_en mem_r_w_en_1 (.icode(icode), .w_enable(mem_r_w_en_1_w_enable), .r_enable(mem_r_w_en_1_r_enable));
  and and_1 (and_1_out, mem_r_w_en_1_r_enable, multiplexer_1_out);
  and and_2 (and_2_out, mem_r_w_en_1_w_enable, multiplexer_5_out);
  Multiplexer multiplexer_3 (
    .in0(multiplexer_1_out), .in1(multiplexer_5_out), .out(multiplexer_3_out), .sel(mem_r_w_en_1_w_enable));
  memData memdata_1 (.valA(valA), .valP(valP), .icode(icode), .mem(memdata_1_mem));
  Counter #(.max('h18), .width(5)) counter_2 (.clk(clk), .Q(counter_2_q));  // open: clr, load, up, count, D, carry
  Register register_1 (.D(memdata_1_mem[7:0]), .en(mem_r_w_en_1_w_enable), .clk(clk), .Q(register_1_q));  // open: clr
  Register register_2 (.D(memdata_1_mem[15:8]), .en(mem_r_w_en_1_w_enable), .clk(clk), .Q(register_2_q));  // open: clr
  Register register_3 (.D(memdata_1_mem[23:16]), .en(mem_r_w_en_1_w_enable), .clk(clk), .Q(register_3_q));  // open: clr
  Register register_4 (.D(memdata_1_mem[31:24]), .en(mem_r_w_en_1_w_enable), .clk(clk), .Q(register_4_q));  // open: clr
  Register register_5 (.D(memdata_1_mem[39:32]), .en(mem_r_w_en_1_w_enable), .clk(clk), .Q(register_5_q));  // open: clr
  Register register_6 (.D(memdata_1_mem[47:40]), .en(mem_r_w_en_1_w_enable), .clk(clk), .Q(register_6_q));  // open: clr
  Register register_7 (.D(memdata_1_mem[55:48]), .en(mem_r_w_en_1_w_enable), .clk(clk), .Q(register_7_q));  // open: clr
  Register register_8 (.D(memdata_1_mem[63:56]), .en(mem_r_w_en_1_w_enable), .clk(clk), .Q(register_8_q));  // open: clr
  memAddr memaddr_1 (.clk(clk), .valE(ValE), .valA(valA), .en(multiplexer_3_out), .icode(icode), .addr(memaddr_1_addr));
  Multiplexer #(.select(4), .width(8)) multiplexer_4 (
    .in0(register_1_q), .in1(register_2_q), .in2(register_3_q), .in3(register_4_q), .in4(register_5_q),
    .in5(register_6_q), .in6(register_7_q), .in7(register_8_q), .out(multiplexer_4_out), .sel(counter_3_q));  // open: in8, in9, in10, in11, in12, in13, in14, in15
  Multiplexer #(.select(5)) multiplexer_5 (
    .in0(1'b0), .in1(1'b0), .in2(1'b0), .in3(1'b0), .in4(1'b0), .in5(1'b0), .in6(1'b0), .in7(1'b0),
    .in8(1'b0), .in9(1'b0), .in10(1'b0), .in11(1'b0), .in12(1'b0), .in13(1'b0), .in14(1'b0), .in15(1'b0),
    .in16(1'b1), .in17(1'b1), .in18(1'b1), .in19(1'b1), .in20(1'b1), .in21(1'b1), .in22(1'b1), .in23(1'b1),
    .in24(1'b0), .out(multiplexer_5_out), .sel(counter_2_q));  // open: in25, in26, in27, in28, in29, in30, in31
  RAM #(.addrWidth(12)) ram_1 (
    .addr(memaddr_1_addr), .we(and_2_out), .oe(and_1_out), .clk(clk), .din(multiplexer_4_out),
    .dout(ram_1_dout));
  Counter #(.max('h7), .width(4)) counter_3 (
    .count(multiplexer_5_out), .clk(clk), .D(4'b0000), .Q(counter_3_q));  // open: clr, load, up, carry
  Register register_9 (.D(ram_1_dout), .en(decoder_1_out0), .clk(clk), .Q(valM[7:0]));  // open: clr
  Register register_10 (.D(ram_1_dout), .en(decoder_1_out1), .clk(clk), .Q(valM[15:8]));  // open: clr
  Register register_11 (.D(ram_1_dout), .en(decoder_1_out2), .clk(clk), .Q(valM[23:16]));  // open: clr
  Register register_12 (.D(ram_1_dout), .en(decoder_1_out3), .clk(clk), .Q(valM[31:24]));  // open: clr
  Register register_13 (.D(ram_1_dout), .en(decoder_1_out4), .clk(clk), .Q(valM[39:32]));  // open: clr
  Register register_14 (.D(ram_1_dout), .en(decoder_1_out5), .clk(clk), .Q(valM[47:40]));  // open: clr
  Register register_15 (.D(ram_1_dout), .en(decoder_1_out6), .clk(clk), .Q(valM[55:48]));  // open: clr
  Register register_16 (.D(ram_1_dout), .en(decoder_1_out7), .clk(clk), .Q(valM[63:56]));  // open: clr
  Counter #(.max('h7), .width(4)) counter_4 (
    .count(multiplexer_2_out), .clk(clk), .Q(counter_4_q));  // open: clr, load, up, D, carry
  Decoder #(.select(4)) decoder_1 (
    .out0(decoder_1_out0), .out1(decoder_1_out1), .out2(decoder_1_out2), .out3(decoder_1_out3),
    .out4(decoder_1_out4), .out5(decoder_1_out5), .out6(decoder_1_out6), .out7(decoder_1_out7),
    .sel(counter_4_q), .en(multiplexer_2_out));  // open: out8, out9, out10, out11, out12, out13, out14, out15

  // Notes on the sheet:
  //   reading mux
  //   mem enable
  //   writing to memory
  //   will either read or write starting cycle 15
  //   reading from memory
endmodule

module memData (
  input  [63:0] valA,
  input  [11:0] valP,
  input  [3:0] icode,
  output [63:0] mem
);

  Multiplexer #(.select(4), .width(64)) multiplexer_1 (
    .in4(valA), .in8({{52{1'b0}}, valP}), .in10(valA), .out(mem), .sel(icode));  // open: in0, in1, in2, in3, in5, in6, in7, in9, in11, in12, in13, in14, in15

  // Notes on the sheet:
  //   change to 64 bit
  //   total 64 bit data
endmodule

module memAddr (
  input  clk,
  input  [63:0] valE,
  input  [63:0] valA,
  input  en,
  input  [3:0] icode,
  output [11:0] addr
);

  wire counter_1_carry;
  wire [11:0] counter_1_q, multiplexer_1_out, subtractor_1_out;

  Multiplexer #(.enable("true"), .select(4), .width(12)) multiplexer_1 (
    .in4(valE[11:0]), .in5(valE[11:0]), .in8(valE[11:0]), .in9(valA[11:0]), .in10(valE[11:0]),
    .in11(valA[11:0]), .out(multiplexer_1_out), .sel(icode), .en(en));  // open: in0, in1, in2, in3, in6, in7, in12, in13, in14, in15
  Counter #(.max('h7), .width(12)) counter_1 (
    .count(en), .clk(clk), .carry(counter_1_carry), .Q(counter_1_q));  // open: clr, load, up, D
  Subtractor #(.width(12)) subtractor_1 (
    .a(multiplexer_1_out), .b({12{1'b0}}), .out(subtractor_1_out));  // open: bin, bout
  Adder #(.width(12)) adder_1 (.a(counter_1_q), .b(subtractor_1_out), .out(addr));  // open: cin, cout

  // Notes on the sheet:
  //   which one will be used as address
endmodule

module mem_r_w_en (
  input  [3:0] icode,
  output w_enable,
  output r_enable
);

  wire decoder_1_out4, decoder_1_out5, decoder_1_out8, decoder_1_out9, decoder_1_out10, decoder_1_out11;

  Decoder #(.select(4)) decoder_1 (
    .out4(decoder_1_out4), .out5(decoder_1_out5), .out8(decoder_1_out8), .out9(decoder_1_out9),
    .out10(decoder_1_out10), .out11(decoder_1_out11), .sel(icode));  // open: out0, out1, out2, out3, out6, out7, out12, out13, out14, out15, en
  or or_1 (w_enable, decoder_1_out4, decoder_1_out8, decoder_1_out10);
  or or_2 (r_enable, decoder_1_out5, decoder_1_out9, decoder_1_out11);

  // Notes on the sheet:
  //   decides read or write based on icode
endmodule

module pcUpdate (
  input  clk,
  input  [11:0] valP,
  input  [63:0] valC,
  input  [63:0] valM,
  input  [3:0] icode,
  input  cnd,
  output [11:0] newPC
);

  wire multiplexer_1_out;
  wire [7:0] counter_1_q;
  wire [11:0] multiplexer_2_out;

  Counter #(.max('h18)) counter_1 (.clk(clk), .Q(counter_1_q));  // open: clr, load, up, count, D, carry
  Multiplexer #(.select(5)) multiplexer_1 (
    .in0(1'b0), .in1(1'b0), .in2(1'b0), .in3(1'b0), .in4(1'b0), .in5(1'b0), .in6(1'b0), .in7(1'b0),
    .in8(1'b0), .in9(1'b0), .in10(1'b0), .in11(1'b0), .in12(1'b0), .in13(1'b0), .in14(1'b0), .in15(1'b0),
    .in16(1'b0), .in17(1'b0), .in18(1'b0), .in19(1'b0), .in20(1'b0), .in21(1'b0), .in22(1'b0), .in23(1'b0),
    .in24(1'b1), .in25(1'b0), .in26(1'b0), .in27(1'b0), .in28(1'b0), .in29(1'b0), .in30(1'b0), .in31(1'b0),
    .out(multiplexer_1_out), .sel(counter_1_q[4:0]));
  Multiplexer #(.enable("true"), .width(12)) multiplexer_2 (
    .in0(valP), .in1(valC[11:0]), .out(multiplexer_2_out), .sel(cnd), .en(multiplexer_1_out));
  Multiplexer #(.enable("true"), .select(4), .width(12)) multiplexer_3 (
    .in0({12{1'b0}}), .in2(valP), .in3(valP), .in4(valP), .in5(valP), .in6(valP), .in7(multiplexer_2_out),
    .in8(valC[11:0]), .in9(valM[11:0]), .in10(valP), .in11(valP), .out(newPC), .sel(icode),
    .en(multiplexer_1_out));  // open: in1, in12, in13, in14, in15

  // Notes on the sheet:
  //   take the last 12 bits
endmodule

module WriteBack (
  input  [3:0] rA,
  input  [3:0] rB,
  input  [3:0] icode,
  output [3:0] dstE,
  output [3:0] dstM
);

  Multiplexer #(.select(4), .width(4)) multiplexer_1 (
    .in0(4'b1111), .in1(4'b1111), .in2(4'b1111), .in3(rB), .in4(4'b1111), .in5(rA), .in6(rB), .in7(4'b1111),
    .in8(4'b0100), .in9(4'b0100), .in10(4'b0100), .in11(rA), .in12(4'b1111), .in13(4'b1111), .in14(4'b1111),
    .in15(4'b1111), .out(dstE), .sel(icode));

  assign dstM = dstE;

  // Notes on the sheet:
  //   popq
  //   figure our popq. INCOMPLETE
endmodule

module testmain (
  input  clk,
  input  [11:0] pc,
  output [63:0] ra,
  output [63:0] rb
);

  wire fetch_1_p3, fetch_1_p4, fetch_1_p5, fetch_1_p6, fetch_1_p7, pcupdate_1_p4;

  // Fetch fetch_1: pin names not known; wires that end beside it: clk, pc, fetch_1_p3, fetch_1_p4, fetch_1_p5, fetch_1_p6, fetch_1_p7, fetch_1_p7, fetch_1_p7
  // pcUpdate pcupdate_1: pin names not known; wires that end beside it: fetch_1_p3, fetch_1_p7, fetch_1_p4, pcupdate_1_p4
  // Decode decode_1: pin names not known; wires that end beside it: clk, fetch_1_p5, fetch_1_p6, fetch_1_p4, ra, rb, pcupdate_1_p4
endmodule
