// Logisim project lab6.circ as structural Verilog: 6 circuits, main circuit main
// byte2
module main (
  input  clk,
  output [3:0] rA,
  output [3:0] rB,
  output [63:0] valC
);

  wire and_1_out, and_2_out, and_3_out, and_4_out, and_5_out, and_6_out, and_7_out, and_8_out, and_9_out,
       byteenables_1_e1, byteenables_1_e2, byteenables_1_e3, byteenables_1_e4, byteenables_1_e5,
       byteenables_1_e6, byteenables_1_e7, byteenables_1_e8, byteenables_1_e9, needregis_1_needregs,
       needvalc_1_needc;
  wire [3:0] instruction_mem_1_byte1, instruction_mem_1_byte1_2;
  wire [7:0] byte1_q, byte2_q, byte3_q, byte4_q, byte5_q, byte6_q, byte7_q, byte8_q, byte9_q,
       instruction_mem_1_byte0, instruction_mem_1_byte2, instruction_mem_1_byte3, instruction_mem_1_byte4,
       instruction_mem_1_byte5, instruction_mem_1_byte6, instruction_mem_1_byte7, instruction_mem_1_byte8,
       instruction_mem_1_byte9;

  instruction_mem instruction_mem_1 (
    .byte0(instruction_mem_1_byte0), .byte1({instruction_mem_1_byte1_2, instruction_mem_1_byte1}),
    .byte2(instruction_mem_1_byte2), .byte3(instruction_mem_1_byte3), .byte4(instruction_mem_1_byte4),
    .byte5(instruction_mem_1_byte5), .byte6(instruction_mem_1_byte6), .byte7(instruction_mem_1_byte7),
    .byte8(instruction_mem_1_byte8), .byte9(instruction_mem_1_byte9));  // open: PC_address
  InstrValid instrvalid_1 (.icode(instruction_mem_1_byte0[7:4]));
  needRegis needregis_1 (.icode(instruction_mem_1_byte0[7:4]), .needRegs(needregis_1_needregs));
  needValC needvalc_1 (.icode(instruction_mem_1_byte0[7:4]), .needC(needvalc_1_needc));
  Register #(.width(4)) register_1 (
    .D(instruction_mem_1_byte1_2), .en(needregis_1_needregs), .clk(clk), .Q(rA));  // open: clr
  Register #(.width(4)) register_2 (
    .D(instruction_mem_1_byte1), .en(needregis_1_needregs), .clk(clk), .Q(rB));  // open: clr
  byteEnables byteenables_1 (
    .needRegs(needregis_1_needregs), .e1(byteenables_1_e1), .e2(byteenables_1_e2), .e3(byteenables_1_e3),
    .e4(byteenables_1_e4), .e5(byteenables_1_e5), .e6(byteenables_1_e6), .e7(byteenables_1_e7),
    .e8(byteenables_1_e8), .e9(byteenables_1_e9));
  and and_1 (and_1_out, needvalc_1_needc, byteenables_1_e1);
  and and_2 (and_2_out, needvalc_1_needc, byteenables_1_e2);
  and and_3 (and_3_out, needvalc_1_needc, byteenables_1_e3);
  and and_4 (and_4_out, needvalc_1_needc, byteenables_1_e4);
  and and_5 (and_5_out, needvalc_1_needc, byteenables_1_e5);
  and and_6 (and_6_out, needvalc_1_needc, byteenables_1_e6);
  and and_7 (and_7_out, needvalc_1_needc, byteenables_1_e7);
  and and_8 (and_8_out, needvalc_1_needc, byteenables_1_e8);
  and and_9 (and_9_out, needvalc_1_needc, byteenables_1_e9);
  Register byte1 (
    .D({instruction_mem_1_byte1_2, instruction_mem_1_byte1}), .en(and_1_out), .clk(clk), .Q(byte1_q));  // open: clr
  Register byte2 (.D(instruction_mem_1_byte2), .en(and_2_out), .clk(clk), .Q(byte2_q));  // open: clr
  Register byte3 (.D(instruction_mem_1_byte3), .en(and_3_out), .clk(clk), .Q(byte3_q));  // open: clr
  Register byte4 (.D(instruction_mem_1_byte4), .en(and_4_out), .clk(clk), .Q(byte4_q));  // open: clr
  Register byte5 (.D(instruction_mem_1_byte5), .en(and_5_out), .clk(clk), .Q(byte5_q));  // open: clr
  Register byte6 (.D(instruction_mem_1_byte6), .en(and_6_out), .clk(clk), .Q(byte6_q));  // open: clr
  Register byte7 (.D(instruction_mem_1_byte7), .en(and_7_out), .clk(clk), .Q(byte7_q));  // open: clr
  Register byte8 (.D(instruction_mem_1_byte8), .en(and_8_out), .clk(clk), .Q(byte8_q));  // open: clr
  Register byte9 (.D(instruction_mem_1_byte9), .en(and_9_out), .clk(clk), .Q(byte9_q));  // open: clr
  Multiplexer #(.width(64)) multiplexer_1 (
    .in0({byte9_q, byte8_q, byte7_q, byte6_q, byte5_q, byte4_q, byte3_q, byte2_q}),
    .in1({byte8_q, byte7_q, byte6_q, byte5_q, byte4_q, byte3_q, byte2_q, byte1_q}), .out(valC),
    .sel(byteenables_1_e1));

  // Notes on the sheet:
  //   icode
  //   w byte 9
  //   w byte 1
endmodule

module instruction_mem (
  input  [11:0] PC_address,
  output [7:0] byte0,
  output [7:0] byte1,
  output [7:0] byte2,
  output [7:0] byte3,
  output [7:0] byte4,
  output [7:0] byte5,
  output [7:0] byte6,
  output [7:0] byte7,
  output [7:0] byte8,
  output [7:0] byte9
);

  ROM #(.addrWidth(12), .dataWidth(40)) rom_1 (.addr(PC_address), .data({byte4, byte3, byte2, byte1, byte0}));
  ROM #(.addrWidth(12), .dataWidth(40)) rom_2 (.addr(PC_address), .data({byte9, byte8, byte7, byte6, byte5}));

  // Notes on the sheet:
  //   contents of rom_1 (hex, n*v repeats v):
  //   8870
  //   instruction memory
endmodule

module needRegis (
  input  [3:0] icode,
  output needRegs
);

  wire comparator_1_eq, comparator_2_eq, comparator_3_eq, comparator_4_eq, comparator_5_eq, comparator_6_eq,
       comparator_7_eq;

  Comparator #(.width(4)) comparator_1 (.a(icode), .b(4'b1010), .eq(comparator_1_eq));  // open: gt, lt
  Comparator #(.width(4)) comparator_2 (.a(icode), .b(4'b0010), .eq(comparator_2_eq));  // open: gt, lt
  Comparator #(.width(4)) comparator_3 (.a(icode), .b(4'b0100), .eq(comparator_3_eq));  // open: gt, lt
  Comparator #(.width(4)) comparator_4 (.a(icode), .b(4'b0101), .eq(comparator_4_eq));  // open: gt, lt
  Comparator #(.width(4)) comparator_5 (.a(icode), .b(4'b1011), .eq(comparator_5_eq));  // open: gt, lt
  Comparator #(.width(4)) comparator_6 (.a(icode), .b(4'b0110), .eq(comparator_6_eq));  // open: gt, lt
  Comparator #(.width(4)) comparator_7 (.a(icode), .b(4'b0011), .eq(comparator_7_eq));  // open: gt, lt
  or or_1 (needRegs, comparator_1_eq, comparator_2_eq, comparator_3_eq, comparator_4_eq, comparator_5_eq, comparator_6_eq, comparator_7_eq);
endmodule

module needValC (
  input  [3:0] icode,
  output needC
);

  wire comparator_1_eq, comparator_2_eq, comparator_3_eq, comparator_4_eq, comparator_5_eq;

  Comparator #(.width(4)) comparator_1 (.a(icode), .b(4'b0011), .eq(comparator_1_eq));  // open: gt, lt
  Comparator #(.width(4)) comparator_2 (.a(icode), .b(4'b0100), .eq(comparator_2_eq));  // open: gt, lt
  Comparator #(.width(4)) comparator_3 (.a(icode), .b(4'b0101), .eq(comparator_3_eq));  // open: gt, lt
  Comparator #(.width(4)) comparator_4 (.a(icode), .b(4'b0111), .eq(comparator_4_eq));  // open: gt, lt
  Comparator #(.width(4)) comparator_5 (.a(icode), .b(4'b1000), .eq(comparator_5_eq));  // open: gt, lt
  or or_1 (needC, comparator_1_eq, comparator_2_eq, comparator_3_eq, comparator_4_eq, comparator_5_eq);
endmodule

module InstrValid (
  input  [3:0] icode
);
endmodule

module byteEnables (
  input  needRegs,
  output e1,
  output e2,
  output e3,
  output e4,
  output e5,
  output e6,
  output e7,
  output e8,
  output e9
);

  not not_1 (e1, needRegs);

  assign e2 = 1'b1;
  assign e3 = 1'b1;
  assign e4 = 1'b1;
  assign e5 = 1'b1;
  assign e6 = 1'b1;
  assign e7 = 1'b1;
  assign e8 = 1'b1;
  assign e9 = needRegs;
endmodule
